# Fritzing sketch KgDashCircuit (saved by Fritzing 0.9.3b)
breadboards: 1

parts:
  R1 = Resistor [tolerance=±5% resistance=100k package=THT]
  C1 = Electrolytic Capacitor [capacitance=1µF package="100 mil [THT, electrolytic]"]
  Car_Power_Supply = Battery block 9V
  D1 = MBR745 Schottky [part_number=1N5822 package="TO220 [THT]"]
  R2 = Resistor [tolerance=±5% resistance=10k package=THT]
  Part1 = Arduino Uno (Rev3)
  Q1 = TRANSISTOR_NPN [package=to-92-ammo]

nets:
  N1: R1.Pin_1, R2.Pin_0, Part1.A0, Q1.B
  N2: C1.+, D1.Cathode, Part1.VIN
  N3: Car_Power_Supply.-, D1.Anode
  GND: Car_Power_Supply.+, Part1.GND
  N4: Part1.D2, Q1.E
  N5: Part1.5V, Q1.C
